// Digital circuit four_bit_adder.dig as structural Verilog
module four_bit_adder (
  input  [3:0] a,
  input  [3:0] b,
  input  cin,
  output cout,
  output overfl,
  output [3:0] y
);

  wire full_adder_1_p3, full_adder_2_p3, full_adder_3_p3;

  // full_adder full_adder_1: pin names not known; wires that end beside it: a[3], b[3], full_adder_1_p3, y[3], cout
  // full_adder full_adder_2: pin names not known; wires that end beside it: a[2], b[2], full_adder_2_p3, y[2], full_adder_1_p3
  // full_adder full_adder_3: pin names not known; wires that end beside it: a[1], b[1], full_adder_3_p3, y[1], full_adder_2_p3
  // full_adder full_adder_4: pin names not known; wires that end beside it: a[0], b[0], cin, y[0], full_adder_3_p3
  xor xor_1 (overfl, cout, full_adder_1_p3);
endmodule
